# Fritzing sketch Prototipoa (saved by Fritzing 0.9.3b)
breadboards: 1

parts:
  Componente1 = iceZUM Alhambra
  U1 = QRD1114 [package=qrd1114]
  U2 = QRD1114 [package=qrd1114]
  M1 = DC Motor
  M2 = DC Motor
  BAT1 = BC9VPC [package=bc9vpc]
  R1 = Resistor [tolerance=±5% resistance=220 package="0402 [SMD]"]
  R2 = Resistor [tolerance=±5% resistance=10k package="0402 [SMD]"]
  R3 = Resistor [tolerance=±5% resistance=220 package="0402 [SMD]"]
  R4 = Resistor [tolerance=±5% resistance=10k package="0402 [SMD]"]
  IC1 = L293D [package=THT]
  J1 = Power Jack [package=power_jack_slot]

nets:
  N1: Componente1.D1, IC1.In_1
  N2: Componente1.D2, IC1.In_2
  N3: Componente1.D3, IC1.In_3
  N4: Componente1.D4, IC1.In_4
  N5: Componente1.D5, U2.E, R2.Pin_0
  N6: Componente1.D6, Componente1.V6, U1.E, R4.Pin_0
  N7: Componente1.GD2, Componente1.GND, U1.K, U2.K, R2.Pin_1, R4.Pin_1, IC1.0V, IC1.Enable_2
  N8: Componente1.5V, U1.C, U2.C, R1.Pin_1, R3.Pin_1, IC1.Enable_1, IC1.+V
  N9: Componente1.VIN, IC1.+Vmotor
  N10: U1.A, R3.Pin_0
  N11: U2.A, R1.Pin_0
  N12: M1.pin_1, IC1.Out_1_(_Controlled_by_Enable_1_)
  N13: M1.pin_2, IC1.Out_2_(_Controlled_by_Enable_1_)
  N14: M2.pin_1, IC1.Out_3_(_Controlled_by_Enable_2_)
  N15: M2.pin_2, IC1.Out_4_(_Controlled_by_Enable_2_)
  N16: BAT1.V+, J1.GNDBREAK
  N17: BAT1.V-, J1.GND

notes:
  JACK ICEZUM

custom parts:
  iceZUM Alhambra: Arduino/zum compatible Open FPGA electronic board. Synthesize hardware easily, using only open source tools
